// Logisim project SAP-1.1.circ as structural Verilog: 11 circuits, main circuit main
module main (
);

  SAP_1 sap_1_1 ();  // open: Test_Input, in_2, Clear_Counter, Clear_Instr__Reg, Clear_C_S, Cp, Ep, nLm, nCE, nLi, nEi, nLa, Ea, Su, Eu, nLb, nLo, WBus_L, WBus_U, Output
endmodule

module SAP_1 (
  input  [7:0] Test_Input,
  input  in_2,
  input  Clear_Counter,
  input  Clear_Instr__Reg,
  input  Clear_C_S,
  input  Cp,
  input  Ep,
  input  nLm,
  input  nCE,
  input  nLi,
  input  nEi,
  input  nLa,
  input  Ea,
  input  Su,
  input  Eu,
  input  nLb,
  input  nLo,
  output [3:0] WBus_L,
  output [3:0] WBus_U,
  output [7:0] Output
);

  wire clock_1_out, not_1_out;
  wire [3:0] instruction_register_1_cs_output, memory_address_register_1_out_4;
  wire [7:0] a_register_1_alu_output, b_register_1_output;
  wire [11:0] controller_sequencer_1_control_word_out;

  assign {WBus_L, WBus_U} = in_2 ? Test_Input : 8'bz;  // Controlled_Buffer controlled_buffer_1
  not not_1 (not_1_out, nCE);
  Controller_sequencer controller_sequencer_1 (
    .Clear(Clear_C_S), .IR_Input(instruction_register_1_cs_output), .nClock(clock_1_out),
    .Control_Word_Out(controller_sequencer_1_control_word_out));
  Program_Counter program_counter_1 (
    .Count(Cp), .Clear(Clear_Counter), .Enable(Ep), .Clock(clock_1_out), .out_5(WBus_U));
  Memory_Address_Register memory_address_register_1 (
    .Load(nLm), .Clock(clock_1_out), .out_4(memory_address_register_1_out_4), .Input(WBus_U));
  RAM #(.addrWidth(4), .dataWidth(8), .bus("combined")) ram_1 (
    .addr(memory_address_register_1_out_4), .data({WBus_L, WBus_U}), .sel(not_1_out), .clk(clock_1_out));  // open: ld, clr
  Instruction_Register instruction_register_1 (
    .nLoad(nLi), .Clear(Clear_Instr__Reg), .nEnable(nEi), .Clock(clock_1_out),
    .CS_Output(instruction_register_1_cs_output), .Input({WBus_L, WBus_U}), .Bus_Output(WBus_U));
  Clock #(.highDuration(1), .lowDuration(1)) clock_1 (.out(clock_1_out));
  A_Register a_register_1 (
    .Input({WBus_U, WBus_L}), .Bus_Output({WBus_U, WBus_L}), .Clock(clock_1_out),
    .ALU_Output(a_register_1_alu_output), .Load(nLa), .Enable(Ea));
  Adder_Subtractor adder_subtractor_1 (
    .Output({WBus_U, WBus_L}), .A_Input(a_register_1_alu_output), .B_Input(b_register_1_output),
    .Subtract(Su), .Enable(Eu));
  B_Register b_register_1 (.Input({WBus_U, WBus_L}), .Output(b_register_1_output), .Clock(clock_1_out), .Load(nLb));
  Output_Register output_register_1 (.Input({WBus_L, WBus_U}), .Clock(clock_1_out), .Output(Output), .Load(nLo));

  // Notes on the sheet:
  //   SAP-1
  //   PC
  //   MAR
  //   IR
  //   C/S
  //   A
  //   A/S
  //   B
  //   O
endmodule

module A_Register (
  input  [7:0] Input,
  input  Load,
  input  Clock,
  input  Enable,
  output [7:0] Bus_Output,
  output [7:0] ALU_Output
);

  wire not_1_out;

  Register #(.width(8), .trigger("rising")) register_1 (
    .D(Input), .en(not_1_out), .Q(ALU_Output), .clk(Clock));  // open: clr
  not not_1 (not_1_out, Load);
  assign Bus_Output = Enable ? ALU_Output : 8'bz;  // Controlled_Buffer controlled_buffer_1
endmodule

module Adder_Subtractor (
  input  [7:0] A_Input,
  input  [7:0] B_Input,
  input  Subtract,
  input  Enable,
  output [7:0] Output
);

  wire not_1_out;
  wire [7:0] adder_1_out, controlled_buffer_1_out, controlled_buffer_2_out;

  assign controlled_buffer_1_out = not_1_out ? B_Input : 8'bz;  // Controlled_Buffer controlled_buffer_1
  not not_1 (not_1_out, Subtract);
  assign controlled_buffer_1_out = ~controlled_buffer_2_out;  // NOT_Gate not_2, 8 bits wide
  assign controlled_buffer_2_out = Subtract ? B_Input : 8'bz;  // Controlled_Buffer controlled_buffer_2
  Adder #(.width(8)) adder_1 (
    .a(A_Input), .b(controlled_buffer_1_out), .out(adder_1_out), .cin(Subtract));  // open: cout
  assign Output = Enable ? adder_1_out : 8'bz;  // Controlled_Buffer controlled_buffer_3
endmodule

module B_Register (
  input  [7:0] Input,
  input  Load,
  input  Clock,
  output [7:0] Output
);

  wire not_1_out;

  Register #(.width(8), .trigger("rising")) register_1 (
    .D(Input), .en(not_1_out), .Q(Output), .clk(Clock));  // open: clr
  not not_1 (not_1_out, Load);
endmodule

module Output_Register (
  input  [7:0] Input,
  input  Load,
  input  Clock,
  output [7:0] Output
);

  wire not_1_out;

  Register #(.width(8), .trigger("rising")) register_1 (
    .D(Input), .en(not_1_out), .Q(Output), .clk(Clock));  // open: clr
  not not_1 (not_1_out, Load);
endmodule

module Program_Counter (
  input  Clock,
  input  Count,
  input  Clear,
  input  Enable,
  output [3:0] out_5
);

  wire [3:0] counter_1_q;

  Counter #(.width(4), .max(15), .trigger("rising")) counter_1 (
    .count(Count), .Q(counter_1_q), .clk(Clock), .clr(Clear));  // open: load, D, carry
  assign out_5 = Enable ? counter_1_q : 4'bz;  // Controlled_Buffer controlled_buffer_1
endmodule

module Memory_Address_Register (
  input  Clock,
  input  [3:0] Input,
  input  Load,
  output [3:0] out_4
);

  wire not_1_out;

  not not_1 (not_1_out, Load);
  Register #(.width(4), .trigger("rising")) register_1 (
    .D(Input), .en(not_1_out), .Q(out_4), .clk(Clock));  // open: clr
endmodule

module Instruction_Register (
  input  Clock,
  input  [7:0] Input,
  input  nLoad,
  input  Clear,
  input  nEnable,
  output [3:0] Bus_Output,
  output [3:0] CS_Output
);

  wire not_1_out, not_2_out;
  wire [3:0] register_1_q;

  Register #(.width(8), .trigger("rising")) register_1 (
    .D(Input), .en(not_1_out), .Q({CS_Output, register_1_q}), .clk(Clock), .clr(Clear));
  not not_1 (not_1_out, nLoad);
  assign Bus_Output = not_2_out ? register_1_q : 4'bz;  // Controlled_Buffer controlled_buffer_1
  not not_2 (not_2_out, nEnable);
endmodule

module Controller_sequencer (
  input  [3:0] IR_Input,
  input  nClock,
  input  Clear,
  output [11:0] Control_Word_Out
);

  wire nor_1_out, not_1_out, not_2_out, not_3_out, or_1_out, shift_register_1_q0, shift_register_1_q1,
       shift_register_1_q2, shift_register_1_q3, shift_register_1_q4;
  wire [3:0] counter_1_q, rom_1_data;

  nor nor_1 (nor_1_out, shift_register_1_q4, shift_register_1_q3, shift_register_1_q2, shift_register_1_q1, shift_register_1_q0);
  Shift_Register #(.width(1), .length(6), .parallel("true"), .trigger("rising")) shift_register_1 (
    .shift(1'b1), .in(nor_1_out), .clk(not_1_out), .clr(Clear), .q0(shift_register_1_q0),
    .q1(shift_register_1_q1), .q2(shift_register_1_q2), .q3(shift_register_1_q3), .q4(shift_register_1_q4));  // open: out, load, d0, d1, d2, d3, d4, d5, q5
  not not_1 (not_1_out, nClock);
  not not_2 (not_2_out, shift_register_1_q2);
  or or_1 (or_1_out, shift_register_1_q0, Clear);
  ROM #(.addrWidth(4), .dataWidth(4)) rom_1 (.addr(IR_Input), .data(rom_1_data));  // open: sel
  not not_3 (not_3_out, nClock);
  ROM #(.addrWidth(4), .dataWidth(12)) rom_2 (.addr(counter_1_q), .data(Control_Word_Out));  // open: sel
  Counter #(.width(4), .max(15), .trigger("rising")) counter_1 (
    .load(shift_register_1_q2), .D(rom_1_data), .count(not_2_out), .Q(counter_1_q), .clk(not_3_out),
    .clr(or_1_out));  // open: carry

  // Notes on the sheet:
  //   Ring Counter
  //   Address ROM
  //   Control ROM
  //   contents of rom_1 (hex, n*v repeats v):
  //   3 6 9 11*0 c
  //   contents of rom_2 (hex, n*v repeats v):
  //   5e3 be3 263 1a3 2c3 3e3 1a3 2e1 3c7 1a3 2e1 3cf 3f2 3e3 3e3
  //   Presettable Counter
endmodule

module Old_Adder_sub (
  input  [7:0] A_Input,
  input  [7:0] B_Input,
  input  Su,
  input  Eu,
  output [7:0] Output
);

  wire not_1_out;
  wire [7:0] adder_1_out, controlled_buffer_2_out, subtractor_1_out;

  assign Output = Eu ? controlled_buffer_2_out : 8'bz;  // Controlled_Buffer controlled_buffer_1
  Adder #(.width(8)) adder_1 (.a(A_Input), .b(B_Input), .out(adder_1_out));  // open: cin, cout
  assign controlled_buffer_2_out = not_1_out ? adder_1_out : 8'bz;  // Controlled_Buffer controlled_buffer_2
  assign controlled_buffer_2_out = Su ? subtractor_1_out : 8'bz;  // Controlled_Buffer controlled_buffer_3
  Subtractor #(.width(8)) subtractor_1 (.a(A_Input), .b(B_Input), .out(subtractor_1_out));  // open: bin, bout
  not not_1 (not_1_out, Su);
endmodule
