// Logisim project ringCounter2.circ as structural Verilog: 1 circuit, main circuit main
module main (
  input  Clr
);

  wire Clk_out, d_ff_1_q, not_1_out, or_1_out, shift_register_1_out;

  Clock #(.highDuration(1), .lowDuration(1)) Clk (.out(Clk_out));
  not not_1 (not_1_out, Clk_out);
  D_Flip_Flop #(.trigger("rising")) d_ff_1 (
    .clk(not_1_out), .D(Clr), .Q(d_ff_1_q), .preset(Clr));  // open: Qn, en, reset
  or or_1 (or_1_out, d_ff_1_q, shift_register_1_out);
  Shift_Register #(.width(1), .length(6), .parallel("true"), .trigger("rising")) shift_register_1 (
    .in(or_1_out), .clk(not_1_out), .out(shift_register_1_out), .clr(Clr));  // open: shift, load, d0, q0, d1, q1, d2, q2, d3, q3, d4, q4, d5, q5

  // Notes on the sheet:
  //   Ring Counter - Circular Shift Register
endmodule
