// Logisim project ringCounter3.circ as structural Verilog: 1 circuit, main circuit main
module main (
  input  Clk,
  input  Clr
);

  wire nor_1_out, shift_register_1_q0, shift_register_1_q1, shift_register_1_q2, shift_register_1_q3,
       shift_register_1_q4;

  nor nor_1 (nor_1_out, shift_register_1_q4, shift_register_1_q3, shift_register_1_q2, shift_register_1_q1, shift_register_1_q0);
  Shift_Register #(.width(1), .length(6), .parallel("true"), .trigger("rising")) shift_register_1 (
    .shift(1'b1), .in(nor_1_out), .clk(Clk), .clr(Clr), .q0(shift_register_1_q0), .q1(shift_register_1_q1),
    .q2(shift_register_1_q2), .q3(shift_register_1_q3), .q4(shift_register_1_q4));  // open: out, load, d0, d1, d2, d3, d4, d5, q5
endmodule
