// Logisim project Exp3.circ as structural Verilog: 1 circuit, main circuit main
module main (
  input  A,
  input  A_2,
  input  B,
  input  B_2,
  input  C,
  input  C_2,
  input  D,
  input  D_2,
  input  E,
  input  E_2,
  input  F,
  input  F_2,
  input  nE,
  input  nE_2,
  input  nF,
  input  nF_2,
  input  A_3,
  input  A_4,
  input  B_3,
  input  C_3,
  input  D_3,
  input  B_4,
  input  E_3,
  input  F_3,
  input  nE_3,
  input  C_4,
  input  nF_3,
  input  A_5,
  input  B_5,
  input  C_5,
  output L1,
  output L1_2,
  output L2,
  output L2_2,
  output L3,
  output L3_2,
  output L4,
  output L4_2,
  output L1_3,
  output L1_4,
  output L2_3,
  output L3_3,
  output L4_3,
  output out_44
);

  wire and_1_out, and_2_out, and_3_out, and_4_out, and_5_out, not_1_out, not_2_out, not_3_out, not_4_out,
       not_5_out, not_6_out, not_7_out, not_8_out;

  not not_1 (not_1_out, nE);
  not not_2 (not_2_out, nF);
  not not_3 (not_3_out, nE_3);
  not not_4 (not_4_out, nF_3);
  Multiplexer #(.select(1), .width(1)) multiplexer_1 ();  // open: in0, in1, out, sel
  or or_1 (L1, A, B);
  or or_2 (L2, C, D);
  or or_3 (L3, E, F);
  or or_4 (L4, not_1_out, not_2_out);
  nor nor_1 (L1_3, A_3, B_3);
  nor nor_2 (L2_3, C_3, D_3);
  nor nor_3 (L3_3, E_3, F_3);
  nor nor_4 (L4_3, not_3_out, not_4_out);
  not not_5 (not_5_out, nE_2);
  not not_6 (not_6_out, nF_2);
  not not_7 (not_7_out, B_4);
  not not_8 (not_8_out, B_5);
  and and_1 (and_1_out, A_4, B_4);
  and and_2 (and_2_out, A_4, C_4);
  and and_3 (and_3_out, not_7_out, C_4);
  and and_4 (and_4_out, A_5, B_5);
  and and_5 (and_5_out, not_8_out, C_5);
  nand nand_1 (L1_2, A_2, B_2);
  nand nand_2 (L2_2, C_2, D_2);
  nand nand_3 (L3_2, E_2, F_2);
  nand nand_4 (L4_2, not_5_out, not_6_out);
  or or_5 (L1_4, and_1_out, and_2_out, and_3_out);
  or or_6 (out_44, and_4_out, and_5_out);

  // Notes on the sheet:
  //   OR Gates
  //   NOR Gates
  //   (A AND B) OR (~B AND C) = L1
  //   NAND Gates
  //   (A AND B) OR (~B AND C) OR (A AND C) = L1
endmodule
