// Logisim project SAP-registers.circ as structural Verilog
module Output_Register (
  input  [7:0] Input,
  input  Lo,
  input  CLK,
  output [7:0] out_4
);

  wire not_1_out;

  not not_1 (not_1_out, Lo);
  Register #(.width(8), .trigger("rising")) register_1 (.D(Input), .en(not_1_out), .Q(out_4), .clk(CLK));  // open: clr

  // Notes on the sheet:
  //   Output Register
endmodule

module B_Register (
  input  [7:0] Input,
  input  Lb,
  input  CLK,
  output [7:0] out_4
);

  wire not_1_out;

  not not_1 (not_1_out, Lb);
  Register #(.width(8), .trigger("rising")) register_1 (.D(Input), .en(not_1_out), .Q(out_4), .clk(CLK));  // open: clr

  // Notes on the sheet:
  //   B Register
endmodule

module A_Register (
  input  [7:0] Input,
  input  La,
  input  Ea,
  input  CLK,
  output [7:0] out_5
);

  wire not_1_out;
  wire [7:0] register_1_q;

  not not_1 (not_1_out, La);
  Register #(.width(8), .trigger("rising")) register_1 (
    .D(Input), .en(not_1_out), .Q(register_1_q), .clk(CLK));  // open: clr
  assign out_5 = Ea ? register_1_q : 8'bz;  // Controlled_Buffer controlled_buffer_1

  // Notes on the sheet:
  //   A Register
endmodule

module Counter_Register (
  input  [3:0] Input,
  input  Ep,
  input  CLR,
  input  CLK,
  output [3:0] out_5
);

  wire not_1_out;
  wire [3:0] counter_1_q;

  Counter #(.width(4), .max(15), .trigger("rising")) counter_1 (
    .D(Input), .Q(counter_1_q), .clk(CLK), .clr(not_1_out));  // open: load, count, carry
  not not_1 (not_1_out, CLR);
  assign out_5 = Ep ? counter_1_q : 4'bz;  // Controlled_Buffer controlled_buffer_1

  // Notes on the sheet:
  //   Counter Register
endmodule
