// Logisim project ch6.circ as structural Verilog
module Half_Adder (
  input  Half_Adder,
  input  in_2,
  output out_3,
  output out_4
);

  and and_1 (out_3, Half_Adder, in_2);
  xor xor_1 (out_4, in_2, Half_Adder);
endmodule

module Full_Adder (
  input  in_1,
  input  Full_Adder,
  input  in_3,
  output out_4,
  output out_5
);

  wire and_1_out, and_2_out, and_3_out, and_4_out, xor_1_out;

  and and_1 (and_1_out, in_1, in_3);
  and and_2 (and_2_out, Full_Adder, in_1);
  and and_3 (and_3_out, Full_Adder, in_3);
  ExactlyOne xor_1 (.out(xor_1_out), .in0(in_1), .in2(in_3), .in4(Full_Adder));
  and and_4 (and_4_out, in_1, in_3, Full_Adder);
  or or_1 (out_4, and_1_out, and_2_out, and_3_out);
  or or_2 (out_5, xor_1_out, and_4_out);
endmodule

module Binary_Adder (
  input  A0,
  input  A1,
  input  A2,
  input  A3,
  input  B0,
  input  B1,
  input  B2,
  input  B3,
  output S0,
  output S1,
  output S2,
  output S3
);

  wire full_adder_1_p4, full_adder_2_p2, full_adder_2_p5, half_adder_1_out_3;

  Half_Adder half_adder_1 (.Half_Adder(A0), .in_2(B0), .out_3(half_adder_1_out_3), .out_4(S0));
  // Full_Adder full_adder_1: pin names not known; wires that end beside it: half_adder_1_out_3, A1, B1, full_adder_1_p4, S1
  // Full_Adder full_adder_2: pin names not known; wires that end beside it: S2, full_adder_2_p2, A3, B3, full_adder_2_p5, S3
  // Full_Adder full_adder_3: pin names not known; wires that end beside it: S1, full_adder_1_p4, A2, B2, full_adder_2_p2, S2
  LED CARRY (.in(full_adder_2_p5));

  // Notes on the sheet:
  //   HA
  //   FA
endmodule

module Adder_Subtractor (
  input  A0,
  input  A1,
  input  A2,
  input  A3,
  input  B0,
  input  B1,
  input  B2,
  input  B3,
  input  SUB,
  output S0,
  output S1,
  output S2,
  output S3
);

  wire full_adder_1_out_4, full_adder_2_out_4, full_adder_3_out_4, full_adder_4_out_4, xor_1_out, xor_2_out,
       xor_3_out, xor_4_out;

  LED CARRY (.in(full_adder_1_out_4));
  xor xor_1 (xor_1_out, B0, SUB);
  Full_Adder full_adder_1 (
    .out_4(full_adder_1_out_4), .Full_Adder(A0), .in_3(xor_1_out), .out_5(S0), .in_1(full_adder_2_out_4));
  xor xor_2 (xor_2_out, B1, SUB);
  xor xor_3 (xor_3_out, B2, SUB);
  Full_Adder full_adder_2 (
    .out_4(full_adder_2_out_4), .Full_Adder(A1), .in_3(xor_2_out), .out_5(S1), .in_1(full_adder_3_out_4));
  Full_Adder full_adder_3 (
    .out_4(full_adder_3_out_4), .Full_Adder(A2), .in_3(xor_3_out), .out_5(S2), .in_1(full_adder_4_out_4));
  xor xor_4 (xor_4_out, B3, SUB);
  Full_Adder full_adder_4 (.out_4(full_adder_4_out_4), .Full_Adder(A3), .in_3(xor_4_out), .out_5(S3), .in_1(SUB));
endmodule
