// Logisim project octalDecoderSkel.circ as structural Verilog: 1 circuit, main circuit main
module main (
  input  [2:0] in_1,
  input  in_2,
  input  in_3,
  input  in_4
);

  wire and_1_out, and_2_out, and_3_out, and_4_out, and_5_out, and_6_out, and_7_out, and_8_out,
       decoder_1_out0, decoder_1_out1, decoder_1_out2, decoder_1_out3, decoder_1_out4, decoder_1_out5,
       decoder_1_out6, decoder_1_out7, not_1_out, not_2_out, not_3_out;

  not not_1 (not_1_out, in_2);
  not not_2 (not_2_out, in_3);
  LED L0 (.in(decoder_1_out0));
  LED L1 (.in(decoder_1_out1));
  not not_3 (not_3_out, in_4);
  Decoder #(.select(3), .tristate("false")) decoder_1 (
    .out0(decoder_1_out0), .out1(decoder_1_out1), .out2(decoder_1_out2), .out3(decoder_1_out3),
    .out4(decoder_1_out4), .out5(decoder_1_out5), .out6(decoder_1_out6), .out7(decoder_1_out7), .sel(in_1));
  LED L5 (.in(decoder_1_out5));
  LED L4 (.in(decoder_1_out4));
  LED L2 (.in(decoder_1_out2));
  LED L3 (.in(decoder_1_out3));
  LED L6 (.in(decoder_1_out6));
  LED L7 (.in(decoder_1_out7));
  LED led_1 (.in(and_1_out));
  and and_1 (and_1_out, not_3_out, not_2_out, not_1_out);
  LED led_2 (.in(and_2_out));
  and and_2 (and_2_out, in_4, not_2_out, not_1_out);
  LED led_3 (.in(and_3_out));
  and and_3 (and_3_out, not_3_out, in_3, not_1_out);
  and and_4 (and_4_out, in_4, in_3, not_1_out);
  LED led_4 (.in(and_4_out));
  LED led_5 (.in(and_5_out));
  and and_5 (and_5_out, in_4, in_3, in_2);
  LED led_6 (.in(and_6_out));
  and and_6 (and_6_out, in_4, not_2_out, in_2);
  and and_7 (and_7_out, not_3_out, in_3, in_2);
  LED led_7 (.in(and_7_out));
  and and_8 (and_8_out, in_4, in_3, in_2);
  LED led_8 (.in(and_8_out));

  // Notes on the sheet:
  //   Octal Decoder
  //   L0
  //   L1
  //   L2
  //   L3
  //   L4
  //   L5
  //   L6
  //   L7
endmodule
