// Logisim project 1.circ as structural Verilog: 1 circuit, main circuit main
module main (
  input  [7:0] in_1,
  input  in_2,
  output [7:0] out_3
);

  wire clock_1_out;
  wire [7:0] register_1_q;

  Clock #(.highDuration(1), .lowDuration(1)) clock_1 (.out(clock_1_out));
  Register #(.width(8), .trigger("rising")) register_1 (
    .D(in_1), .Q(register_1_q), .clk(clock_1_out));  // open: en, clr
  assign out_3 = in_2 ? register_1_q : 8'bz;  // Controlled_Buffer controlled_buffer_1
endmodule
