// Logisim project regbus.circ as structural Verilog: 2 circuits, main circuit main
module main (
  input  La,
  input  Eb,
  input  Ea,
  input  Lb,
  input  Lc,
  input  Eb_2,
  input  Ec,
  input  Lb_2,
  output [7:0] out_9
);

  wire clock_1_out;
  wire [7:0] A_q, B_2_q, B_q, C_q;

  Register #(.width(8), .trigger("rising")) A (.D(out_9), .en(La), .Q(A_q), .clk(clock_1_out));  // open: clr
  Register #(.width(8), .trigger("rising")) C (.D(out_9), .en(Lc), .Q(C_q), .clk(clock_1_out));  // open: clr
  assign out_9 = Ea ? A_q : 8'bz;  // Controlled_Buffer controlled_buffer_1
  assign out_9 = Ec ? C_q : 8'bz;  // Controlled_Buffer controlled_buffer_2
  Clock #(.highDuration(1), .lowDuration(1)) clock_1 (.out(clock_1_out));
  Register #(.width(8), .trigger("rising")) B (.D(out_9), .en(Lb), .Q(B_q), .clk(clock_1_out));  // open: clr
  Register #(.width(8), .trigger("rising")) B_2 (.D(out_9), .en(Lb_2), .Q(B_2_q), .clk(clock_1_out));  // open: clr
  assign out_9 = Eb ? B_q : 8'bz;  // Controlled_Buffer controlled_buffer_3
  assign out_9 = Eb_2 ? B_2_q : 8'bz;  // Controlled_Buffer controlled_buffer_4

  // Notes on the sheet:
  //   Registers on a Tri-State Bus
  //   8-bit bus
  //   J Bolton
endmodule

module Bus_Driven_Register (
  input  [7:0] Input,
  input  L,
  input  E,
  input  Clock,
  output [7:0] Output
);

  wire [7:0] register_1_q;

  Register #(.width(8), .trigger("rising")) register_1 (.D(Input), .en(L), .Q(register_1_q), .clk(Clock));  // open: clr
  assign Output = E ? register_1_q : 8'bz;  // Controlled_Buffer controlled_buffer_1
endmodule
