// Logisim project registersOnBus.circ as structural Verilog: 1 circuit, main circuit main
module main (
  input  in_1,
  input  in_2,
  input  in_3,
  input  in_4,
  input  in_5,
  input  in_6,
  input  in_7,
  input  in_8,
  output [7:0] out_9
);

  wire clock_1_out;
  wire [7:0] register_1_q, register_2_q, register_3_q, register_4_q;

  Clock #(.highDuration(1), .lowDuration(1)) clock_1 (.out(clock_1_out));
  Register #(.width(8), .trigger("rising")) register_1 (
    .D(out_9), .en(in_3), .Q(register_1_q), .clk(clock_1_out));  // open: clr
  Register #(.width(8), .trigger("rising")) register_2 (
    .D(out_9), .en(in_7), .Q(register_2_q), .clk(clock_1_out));  // open: clr
  assign out_9 = in_4 ? register_1_q : 8'bz;  // Controlled_Buffer controlled_buffer_1
  assign out_9 = in_8 ? register_2_q : 8'bz;  // Controlled_Buffer controlled_buffer_2
  assign out_9 = in_1 ? register_3_q : 8'bz;  // Controlled_Buffer controlled_buffer_3
  assign out_9 = in_5 ? register_4_q : 8'bz;  // Controlled_Buffer controlled_buffer_4
  Register #(.width(8), .trigger("rising")) register_3 (
    .D(out_9), .en(in_2), .Q(register_3_q), .clk(clock_1_out));  // open: clr
  Register #(.width(8), .trigger("rising")) register_4 (
    .D(out_9), .en(in_6), .Q(register_4_q), .clk(clock_1_out));  // open: clr

  // Notes on the sheet:
  //   Registers on Tri-state Bus
endmodule
