// Logisim project registersTransfer.circ as structural Verilog: 1 circuit, main circuit main
module main (
  input  La,
  input  Ea,
  input  Lb,
  input  Eb,
  input  Lc,
  input  Ec,
  input  Ld,
  input  Ed
);

  wire Clk_out;
  wire [7:0] A_q, B_q, C_q, controlled_buffer_1_out, D_q;

  Register #(.width(8), .trigger("rising")) A (
    .D(controlled_buffer_1_out), .en(La), .Q(A_q), .clk(Clk_out));  // open: clr
  Register #(.width(8), .trigger("rising")) B (
    .D(controlled_buffer_1_out), .en(Lb), .Q(B_q), .clk(Clk_out));  // open: clr
  Clock #(.highDuration(1), .lowDuration(1)) Clk (.out(Clk_out));
  assign controlled_buffer_1_out = Ea ? A_q : 8'bz;  // Controlled_Buffer controlled_buffer_1
  assign controlled_buffer_1_out = Eb ? B_q : 8'bz;  // Controlled_Buffer controlled_buffer_2
  assign controlled_buffer_1_out = Ed ? D_q : 8'bz;  // Controlled_Buffer controlled_buffer_3
  assign controlled_buffer_1_out = Ec ? C_q : 8'bz;  // Controlled_Buffer controlled_buffer_4
  Register #(.width(8), .trigger("rising")) D (
    .D(controlled_buffer_1_out), .en(Ld), .Q(D_q), .clk(Clk_out));  // open: clr
  Register #(.width(8), .trigger("rising")) C (
    .D(controlled_buffer_1_out), .en(Lc), .Q(C_q), .clk(Clk_out));  // open: clr

  // Notes on the sheet:
  //   Register Transfer Control
endmodule
