// Logisim project regsubbus.circ as structural Verilog: 2 circuits, main circuit main
module main (
  input  La,
  input  Eb,
  input  Ea,
  input  Lb,
  input  Lc,
  input  Ed,
  input  Ec,
  input  Ld,
  output [7:0] out_9
);

  wire clock_1_out;

  Bus_Driven_Register bus_driven_register_1 (.Input(out_9), .L(La), .E(Ea), .Clock(clock_1_out), .Output(out_9));
  Bus_Driven_Register bus_driven_register_2 (.Input(out_9), .L(Lc), .E(Ec), .Clock(clock_1_out), .Output(out_9));
  Clock #(.highDuration(1), .lowDuration(1)) clock_1 (.out(clock_1_out));
  Bus_Driven_Register bus_driven_register_3 (.Input(out_9), .L(Lb), .E(Eb), .Clock(clock_1_out), .Output(out_9));
  Bus_Driven_Register bus_driven_register_4 (.Input(out_9), .L(Ld), .E(Ed), .Clock(clock_1_out), .Output(out_9));

  // Notes on the sheet:
  //   A
  //   C
  //   Sub-Circuit Registers on a Tri-State Bus
  //   8-bit bus
  //   B
  //   D
  //   J Bolton
endmodule

module Bus_Driven_Register (
  input  [7:0] Input,
  input  L,
  input  E,
  input  Clock,
  output [7:0] Output
);

  wire [7:0] register_1_q;

  Register #(.width(8), .trigger("rising")) register_1 (.D(Input), .en(L), .Q(register_1_q), .clk(Clock));  // open: clr
  assign Output = E ? register_1_q : 8'bz;  // Controlled_Buffer controlled_buffer_1

  // Notes on the sheet:
  //   Bus-Driven Register
  //   J Bolton
endmodule
