// Logisim project SAP-1a.circ as structural Verilog: 13 circuits, main circuit main
module main (
  input  [7:0] Data,
  input  [3:0] Location,
  input  Run,
  output [7:0] _0000_0H,
  output [7:0] _0001_1H,
  output [7:0] _0010_2H,
  output [7:0] _0011_3H,
  output [7:0] _0100_4H,
  output [7:0] _0101_5H,
  output [7:0] _0110_6H,
  output [7:0] _0111_7H,
  output [7:0] _1000_8H,
  output [7:0] _1001_9H,
  output [7:0] _1010_AH,
  output [7:0] Output,
  output [7:0] _1011_BH,
  output [7:0] _1100_CH,
  output [7:0] _1101_DH,
  output [7:0] _1110_EH,
  output [7:0] _1111_FH
);

  Button Load ();  // open: out
  SAP_1 sap_1_1 ();  // open: T_State, in_1, Run

  // Notes on the sheet:
  //   Load
  //   Commands
  //   LDA: 0000
  //   ADD: 0001
  //   SUB: 0002
  //   OUT: 1110
  //   HLT: 1111
  //   RAM
  //   Location
  //   Data
endmodule

module SAP_1 (
  input  in_1,
  input  Run,
  output [5:0] T_State
);

  wire a_register_1_program_counter_load_enable, and_1_out, clock_1_out, instruction_register_1_nhalt,
       not_1_out, not_2_out, not_3_out, or_1_out;
  wire [3:0] controller_sequencer_1_control_word_out_2, instruction_register_1_cs_output,
       memory_address_register_1_ram_output, output_register_1_output, output_register_1_output_2;
  wire [7:0] a_register_1_alu_output, b_register_1_output, ram_1_data;
  wire [15:0] controller_sequencer_1_control_word_out;

  Hex_Digit_Display hex_digit_display_1 (.value(controller_sequencer_1_control_word_out[15:12]));  // open: dp
  not not_1 (not_1_out, controller_sequencer_1_control_word_out[8]);
  not not_2 (not_2_out, controller_sequencer_1_control_word_out[12]);
  Hex_Digit_Display hex_digit_display_2 (.value(controller_sequencer_1_control_word_out[11:8]));  // open: dp
  Hex_Digit_Display hex_digit_display_3 (.value(controller_sequencer_1_control_word_out_2));  // open: dp
  or or_1 (or_1_out, a_register_1_program_counter_load_enable, controller_sequencer_1_control_word_out[13]);
  RAM #(.addrWidth(4), .dataWidth(8), .bus("asynch")) ram_1 (
    .addr(memory_address_register_1_ram_output), .data(ram_1_data), .sel(not_1_out), .ld(not_2_out),
    .clr(in_1));
  Hex_Digit_Display hex_digit_display_4 (.value(controller_sequencer_1_control_word_out[3:0]));  // open: dp
  Program_Counter program_counter_1 (
    .Count(controller_sequencer_1_control_word_out[11]), .Lp(or_1_out),
    .Enable(controller_sequencer_1_control_word_out[10]), .Clock(and_1_out), .Bus_Input(ram_1_data[3:0]),
    .Bus_Output(ram_1_data[3:0]), .Clear(not_3_out));
  Memory_Address_Register memory_address_register_1 (
    .RAM_output(memory_address_register_1_ram_output), .Load(controller_sequencer_1_control_word_out[9]),
    .Input(ram_1_data[3:0]), .Clock(and_1_out));
  Instruction_Register instruction_register_1 (
    .nLoad(controller_sequencer_1_control_word_out_2[3]),
    .nEnable(controller_sequencer_1_control_word_out_2[2]), .CS_Output(instruction_register_1_cs_output),
    .Input(ram_1_data), .Clock(and_1_out), .Bus_Output(ram_1_data[3:0]),
    .nHalt(instruction_register_1_nhalt), .Clear(not_3_out));
  Controller_sequencer controller_sequencer_1 (
    .T_State(T_State), .IR_Input(instruction_register_1_cs_output),
    .Control_Word_Out({controller_sequencer_1_control_word_out[15:8], controller_sequencer_1_control_word_out_2, controller_sequencer_1_control_word_out[3:0]}),
    .Clock(and_1_out), .Clear(not_3_out));
  Clock #(.highDuration(1), .lowDuration(1)) clock_1 (.out(clock_1_out));
  not not_3 (not_3_out, Run);
  and and_1 (and_1_out, clock_1_out, Run, instruction_register_1_nhalt);
  A_Register a_register_1 (
    .Input(ram_1_data), .Bus_Output(ram_1_data), .Clock(and_1_out),
    .Program_Counter_Load_Enable(a_register_1_program_counter_load_enable),
    .ALU_Output(a_register_1_alu_output), .Ta(controller_sequencer_1_control_word_out[14]),
    .Load(controller_sequencer_1_control_word_out_2[1]), .Enable(controller_sequencer_1_control_word_out_2[0]));
  Adder_Subtractor adder_subtractor_1 (
    .Output(ram_1_data), .A_Input(a_register_1_alu_output), .B_Input(b_register_1_output),
    .Subtract(controller_sequencer_1_control_word_out[3]), .Enable(controller_sequencer_1_control_word_out[2]));
  B_Register b_register_1 (
    .Input(ram_1_data), .Clock(and_1_out), .Output(b_register_1_output),
    .Load(controller_sequencer_1_control_word_out[1]));
  Output_Register output_register_1 (
    .Input(ram_1_data), .Clock(and_1_out), .Output({output_register_1_output_2, output_register_1_output}),
    .Load(controller_sequencer_1_control_word_out[0]));
  Hex_Digit_Display hex_digit_display_5 (.value(output_register_1_output));  // open: dp
  Hex_Digit_Display hex_digit_display_6 (.value(output_register_1_output_2));  // open: dp

  // Notes on the sheet:
  //   SAP-1J
  //   Control Word
  //   PC
  //   MAR
  //   IR
  //   C/S
  //   A
  //   A/S
  //   B
  //   O
  //   Output
  //   Load: 0M
  //   Add: 1M
  //   Subtract: 2M
  //   Store: 3M
  //   Jump: 4M
  //   Output: E0
  //   Halt: F0
  //   Jump if Zero: 5M
  //   Load Indirect: 6M
endmodule

module A_Register (
  input  Clock,
  input  [7:0] Input,
  input  Ta,
  input  Load,
  input  Enable,
  output Program_Counter_Load_Enable,
  output [7:0] Bus_Output,
  output [7:0] ALU_Output
);

  wire not_1_out, not_2_out;

  Register #(.width(8), .trigger("rising")) register_1 (
    .D(Input), .en(not_1_out), .Q(ALU_Output), .clk(Clock));  // open: clr
  not not_1 (not_1_out, Load);
  assign Bus_Output = Enable ? ALU_Output : 8'bz;  // Controlled_Buffer controlled_buffer_1
  not not_2 (not_2_out, Ta);
  nor nor_1 (Program_Counter_Load_Enable, ALU_Output[0], ALU_Output[1], ALU_Output[2], ALU_Output[3], ALU_Output[4], ALU_Output[5], ALU_Output[6], ALU_Output[7], not_2_out);

  // Notes on the sheet:
  //   A Register
endmodule

module Adder_Subtractor (
  input  [7:0] A_Input,
  input  [7:0] B_Input,
  input  Subtract,
  input  Enable,
  output [7:0] Output
);

  wire [7:0] adder_1_out, xor_1_out;

  assign xor_1_out = B_Input ^ {8{Subtract}};  // XOR_Gate xor_1, 8 bits wide
  Adder #(.width(8)) adder_1 (.a(xor_1_out), .b(A_Input), .out(adder_1_out), .cin(Subtract));  // open: cout
  assign Output = Enable ? adder_1_out : 8'bz;  // Controlled_Buffer controlled_buffer_1

  // Notes on the sheet:
  //   Adder/Subtracter
endmodule

module B_Register (
  input  [7:0] Input,
  input  Load,
  input  Clock,
  output [7:0] Output
);

  wire not_1_out;

  Register #(.width(8), .trigger("rising")) register_1 (
    .D(Input), .en(not_1_out), .Q(Output), .clk(Clock));  // open: clr
  not not_1 (not_1_out, Load);

  // Notes on the sheet:
  //   B Register
endmodule

module Output_Register (
  input  [7:0] Input,
  input  Load,
  input  Clock,
  output [7:0] Output
);

  wire not_1_out;

  Register #(.width(8), .trigger("rising")) register_1 (
    .D(Input), .en(not_1_out), .Q(Output), .clk(Clock));  // open: clr
  not not_1 (not_1_out, Load);

  // Notes on the sheet:
  //   Output Register
endmodule

module Program_Counter (
  input  Clock,
  input  [3:0] Bus_Input,
  input  Count,
  input  Lp,
  input  Clear,
  input  Enable,
  output [3:0] Bus_Output
);

  wire not_1_out;
  wire [3:0] counter_1_q;

  Counter #(.width(4), .max(15), .trigger("rising")) counter_1 (
    .load(Lp), .D(Bus_Input), .count(Count), .Q(counter_1_q), .clk(not_1_out), .clr(Clear));  // open: carry
  not not_1 (not_1_out, Clock);
  assign Bus_Output = Enable ? counter_1_q : 4'bz;  // Controlled_Buffer controlled_buffer_1

  // Notes on the sheet:
  //   Program Counter
endmodule

module Memory_Address_Register (
  input  [3:0] Input,
  input  Load,
  input  Clock,
  output [3:0] RAM_output
);

  wire not_1_out;

  not not_1 (not_1_out, Load);
  Register #(.width(4), .trigger("rising")) register_1 (
    .D(Input), .en(not_1_out), .Q(RAM_output), .clk(Clock));  // open: clr

  // Notes on the sheet:
  //   MAR
endmodule

module Instruction_Register (
  input  [7:0] Input,
  input  Clock,
  input  nLoad,
  input  nEnable,
  input  Clear,
  output [3:0] Bus_Output,
  output [3:0] CS_Output,
  output nHalt
);

  wire not_1_out, not_2_out;
  wire [3:0] register_1_q;

  Register #(.width(8), .trigger("rising")) register_1 (
    .D(Input), .en(not_1_out), .Q({CS_Output, register_1_q}), .clk(Clock), .clr(Clear));
  not not_1 (not_1_out, nLoad);
  assign Bus_Output = not_2_out ? register_1_q : 4'bz;  // Controlled_Buffer controlled_buffer_1
  not not_2 (not_2_out, nEnable);
  nand nand_1 (nHalt, CS_Output[3], CS_Output[2], CS_Output[1], CS_Output[0]);

  // Notes on the sheet:
  //   Instruction Register
endmodule

module Controller_sequencer (
  input  [3:0] IR_Input,
  input  Clock,
  input  Clear,
  output [15:0] Control_Word_Out,
  output [5:0] T_State
);

  wire not_1_out, or_1_out;
  wire [1:0] t_state_sequencer_1_t6;
  wire [7:0] counter_1_q, multiplexer_1_out, rom_1_data;

  T_State_Sequencer t_state_sequencer_1 (
    .Clock(Clock), .Clear(Clear), .T_State(T_State), .T3(t_state_sequencer_1_t6[1]),
    .T6(t_state_sequencer_1_t6[0]));
  ROM #(.addrWidth(4), .dataWidth(8)) rom_1 (.addr(IR_Input), .data(rom_1_data));  // open: sel
  Multiplexer #(.select(2), .width(8)) multiplexer_1 (
    .in1({8{1'b0}}), .in2(rom_1_data), .out(multiplexer_1_out), .sel(t_state_sequencer_1_t6));  // open: in0, in3
  or or_1 (or_1_out, t_state_sequencer_1_t6[1], t_state_sequencer_1_t6[0]);
  not not_1 (not_1_out, or_1_out);
  Counter #(.width(8), .max(255), .trigger("falling")) counter_1 (
    .load(or_1_out), .D(multiplexer_1_out), .count(not_1_out), .Q(counter_1_q), .clk(Clock), .clr(Clear));  // open: carry
  ROM #(.addrWidth(8), .dataWidth(16)) rom_2 (.addr(counter_1_q), .data(Control_Word_Out));  // open: sel

  // Notes on the sheet:
  //   Controller/sequencer
  //   T-State Sequencer
  //   Address ROM
  //   contents of rom_1 (hex, n*v repeats v):
  //   3 6 9 f 12 15 18 7*0 c
  //   Control ROM
  //   contents of rom_2 (hex, n*v repeats v):
  //   5e3 be3 263 1a3 2c3 3e3 1a3 2e1 3c7 1a3 2e1 3cf 3f2 3e3 3e3 1a3 12f3 3e3 23a3 3e3 3e3 43a3 3e3 3e3
  //   1a3 e3 2c3
  //   Load: 0000/0
  //   Add: 0001/1
  //   Subtract: 0010/2
  //   Store: 0011/3
  //   Jump: 0100/4
  //   Jump if Zero: 01001/5
  //   Output:1110/E
  //   Store: 1111/F
  //   Load Indirect (pointer): 0110/6
endmodule

module T_State_Sequencer (
  input  Clock,
  input  Clear,
  output T3,
  output T6,
  output [5:0] T_State
);

  wire not_1_out;

  not not_1 (not_1_out, Clock);
  D_Flip_Flop #(.trigger("rising")) d_ff_1 (
    .clk(not_1_out), .D(T6), .Q(T_State[5]), .preset(Clear));  // open: Qn, en, reset
  D_Flip_Flop #(.trigger("rising")) d_ff_2 (
    .clk(not_1_out), .D(T_State[5]), .Q(T_State[4]), .reset(Clear));  // open: Qn, preset, en
  D_Flip_Flop #(.trigger("rising")) d_ff_3 (
    .clk(not_1_out), .D(T_State[4]), .Q(T3), .reset(Clear));  // open: Qn, preset, en
  D_Flip_Flop #(.trigger("rising")) d_ff_4 (
    .clk(not_1_out), .D(T3), .Q(T_State[2]), .reset(Clear));  // open: Qn, preset, en
  D_Flip_Flop #(.trigger("rising")) d_ff_5 (
    .clk(not_1_out), .D(T_State[2]), .Q(T_State[1]), .reset(Clear));  // open: Qn, preset, en
  D_Flip_Flop #(.trigger("rising")) d_ff_6 (
    .clk(not_1_out), .D(T_State[1]), .Q(T6), .reset(Clear));  // open: Qn, preset, en

  assign {T_State[3], T_State[0]} = {T3, T6};

  // Notes on the sheet:
  //   T-State Sequencer
endmodule

module Old_Adder_sub (
  input  [7:0] A_Input,
  input  [7:0] B_Input,
  input  Su,
  input  Eu,
  output [7:0] Output
);

  wire not_1_out;
  wire [7:0] adder_1_out, controlled_buffer_2_out, subtractor_1_out;

  assign Output = Eu ? controlled_buffer_2_out : 8'bz;  // Controlled_Buffer controlled_buffer_1
  Adder #(.width(8)) adder_1 (.a(A_Input), .b(B_Input), .out(adder_1_out));  // open: cin, cout
  assign controlled_buffer_2_out = not_1_out ? adder_1_out : 8'bz;  // Controlled_Buffer controlled_buffer_2
  assign controlled_buffer_2_out = Su ? subtractor_1_out : 8'bz;  // Controlled_Buffer controlled_buffer_3
  Subtractor #(.width(8)) subtractor_1 (.a(A_Input), .b(B_Input), .out(subtractor_1_out));  // open: bin, bout
  not not_1 (not_1_out, Su);
endmodule

module Refresh_ram_experiment (
  input  in_1,
  input  in_2,
  input  in_3,
  input  in_4,
  input  in_5,
  output [7:0] _0000_0H,
  output [7:0] _0001_1H,
  output [7:0] _0010_2H,
  output [7:0] _0011_3H,
  output [7:0] _0100_4H,
  output [7:0] _0101_5H,
  output [7:0] _0110_6H,
  output [7:0] _0111_7H,
  output [7:0] _1000_8H,
  output [7:0] _1001_9H,
  output [7:0] _1010_AH,
  output [7:0] _1011_BH,
  output [7:0] _1100_CH,
  output [7:0] _1101_DH,
  output [7:0] _1110_EH,
  output [7:0] _1111_FH
);

  wire [3:0] counter_1_q;
  wire [7:0] demultiplexer_1_out0, demultiplexer_1_out1, demultiplexer_1_out2, demultiplexer_1_out3,
       demultiplexer_1_out4, demultiplexer_1_out5, demultiplexer_1_out6, demultiplexer_1_out7,
       demultiplexer_1_out8, demultiplexer_1_out9, demultiplexer_1_out10, demultiplexer_1_out11,
       demultiplexer_1_out12, demultiplexer_1_out13, demultiplexer_1_out14, demultiplexer_1_out15, ram_1_data;

  Counter #(.width(4), .max(15), .trigger("rising")) counter_1 (.Q(counter_1_q));  // open: load, D, count, carry, clk, clr
  RAM #(.addrWidth(4), .dataWidth(8), .bus("separate")) ram_1 (
    .addr(counter_1_q), .data(ram_1_data), .str(in_1), .sel(in_2), .clk(in_5), .ld(in_3), .clr(in_4));  // open: din
  Demultiplexer #(.select(4), .width(8), .tristate("true")) demultiplexer_1 (
    .out0(demultiplexer_1_out0), .out1(demultiplexer_1_out1), .out2(demultiplexer_1_out2),
    .out3(demultiplexer_1_out3), .out4(demultiplexer_1_out4), .out5(demultiplexer_1_out5),
    .out6(demultiplexer_1_out6), .out7(demultiplexer_1_out7), .out8(demultiplexer_1_out8),
    .out9(demultiplexer_1_out9), .out10(demultiplexer_1_out10), .out11(demultiplexer_1_out11),
    .out12(demultiplexer_1_out12), .out13(demultiplexer_1_out13), .out14(demultiplexer_1_out14),
    .out15(demultiplexer_1_out15), .in(ram_1_data), .sel(counter_1_q));
  Register #(.width(8), .trigger("rising")) register_1 (
    .D(demultiplexer_1_out0), .Q(_0000_0H), .clk(in_5));  // open: en, clr
  Register #(.width(8), .trigger("rising")) register_2 (
    .D(demultiplexer_1_out1), .Q(_0001_1H), .clk(in_5));  // open: en, clr
  Register #(.width(8), .trigger("rising")) register_3 (
    .D(demultiplexer_1_out2), .Q(_0010_2H), .clk(in_5));  // open: en, clr
  Register #(.width(8), .trigger("rising")) register_4 (
    .D(demultiplexer_1_out3), .Q(_0011_3H), .clk(in_5));  // open: en, clr
  Register #(.width(8), .trigger("rising")) register_5 (
    .D(demultiplexer_1_out4), .Q(_0100_4H), .clk(in_5));  // open: en, clr
  Register #(.width(8), .trigger("rising")) register_6 (
    .D(demultiplexer_1_out5), .Q(_0101_5H), .clk(in_5));  // open: en, clr
  Register #(.width(8), .trigger("rising")) register_7 (
    .D(demultiplexer_1_out6), .Q(_0110_6H), .clk(in_5));  // open: en, clr
  Register #(.width(8), .trigger("rising")) register_8 (
    .D(demultiplexer_1_out7), .Q(_0111_7H), .clk(in_5));  // open: en, clr
  Register #(.width(8), .trigger("rising")) register_9 (
    .D(demultiplexer_1_out8), .Q(_1000_8H), .clk(in_5));  // open: en, clr
  Register #(.width(8), .trigger("rising")) register_10 (
    .D(demultiplexer_1_out9), .Q(_1001_9H), .clk(in_5));  // open: en, clr
  Register #(.width(8), .trigger("rising")) register_11 (
    .D(demultiplexer_1_out10), .Q(_1010_AH), .clk(in_5));  // open: en, clr
  Register #(.width(8), .trigger("rising")) register_12 (
    .D(demultiplexer_1_out11), .Q(_1011_BH), .clk(in_5));  // open: en, clr
  Register #(.width(8), .trigger("rising")) register_13 (
    .D(demultiplexer_1_out12), .Q(_1100_CH), .clk(in_5));  // open: en, clr
  Register #(.width(8), .trigger("rising")) register_14 (
    .D(demultiplexer_1_out13), .Q(_1101_DH), .clk(in_5));  // open: en, clr
  Register #(.width(8), .trigger("rising")) register_15 (
    .D(demultiplexer_1_out14), .Q(_1110_EH), .clk(in_5));  // open: en, clr
  Register #(.width(8), .trigger("rising")) register_16 (
    .D(demultiplexer_1_out15), .Q(_1111_FH), .clk(in_5));  // open: en, clr
endmodule
