// Logisim project SAP-1s.circ as structural Verilog
module SAP_1Js (
  input  Run,
  output [5:0] T_State
);

  wire and_1_out, clock_1_out, instruction_register_1_nhalt, not_1_out, not_2_out, or_1_out, stack_1_to_pc;
  wire [3:0] controller_sequencer_1_control_word_out_2, controller_sequencer_1_control_word_out_3,
       instruction_register_1_cs_output, output_register_1_output_2, output_register_1_output_3,
       output_register_1_output_4;
  wire [7:0] controller_sequencer_1_control_word_out, output_register_1_output;
  wire [7:4] controller_sequencer_1_control_word_out_4;
  wire [15:0] memory_address_register_1_ram_output;
  wire [19:0] adder_subtractor_1_out_7, adder_subtractor_1_out_8, ram_1_data;

  Hex_Digit_Display hex_digit_display_1 (.value(controller_sequencer_1_control_word_out_4));  // open: dp
  Hex_Digit_Display hex_digit_display_2 (.value(controller_sequencer_1_control_word_out_3));  // open: dp
  Program_Counter program_counter_1 (
    .Count(controller_sequencer_1_control_word_out_4[7]), .Lp(or_1_out),
    .Enable(controller_sequencer_1_control_word_out_4[5]), .Bus_Input(ram_1_data[19:4]),
    .Bus_Output(ram_1_data[19:4]), .Clock(and_1_out), .Clear(not_2_out));
  Memory_Address_Register memory_address_register_1 (
    .RAM_output(memory_address_register_1_ram_output), .Input(ram_1_data[19:4]), .Clock(and_1_out),
    .Load(controller_sequencer_1_control_word_out_4[4]));
  RAM #(.addrWidth(16), .dataWidth(20), .bus("asynch")) ram_1 (
    .addr(memory_address_register_1_ram_output), .data(ram_1_data),
    .sel(controller_sequencer_1_control_word_out_3[2]), .ld(not_1_out));  // open: clr
  not not_1 (not_1_out, controller_sequencer_1_control_word_out_3[3]);
  Instruction_Register instruction_register_1 (
    .CS_Output(instruction_register_1_cs_output), .Input(ram_1_data), .Clock(and_1_out),
    .Bus_Output(ram_1_data[19:4]), .Load(controller_sequencer_1_control_word_out_3[1]),
    .Enable(controller_sequencer_1_control_word_out_3[0]), .nHalt(instruction_register_1_nhalt),
    .Clear(not_2_out));
  Controller_sequencer controller_sequencer_1 (
    .T_State(T_State), .IR_Input(instruction_register_1_cs_output),
    .Control_Word_Out({controller_sequencer_1_control_word_out_4, controller_sequencer_1_control_word_out_3, controller_sequencer_1_control_word_out_2, controller_sequencer_1_control_word_out}),
    .Clock(and_1_out), .Clear(not_2_out));
  Hex_Digit_Display hex_digit_display_3 (.value(controller_sequencer_1_control_word_out_2));  // open: dp
  Hex_Digit_Display hex_digit_display_4 (.value(controller_sequencer_1_control_word_out[7:4]));  // open: dp
  or or_1 (or_1_out, stack_1_to_pc, controller_sequencer_1_control_word_out_4[6]);
  Hex_Digit_Display hex_digit_display_5 (.value(controller_sequencer_1_control_word_out[3:0]));  // open: dp
  not not_2 (not_2_out, Run);
  and and_1 (and_1_out, instruction_register_1_nhalt, Run, clock_1_out);
  Clock #(.highDuration(1), .lowDuration(1)) clock_1 (.out(clock_1_out));
  Hex_Digit_Display hex_digit_display_6 (.value(output_register_1_output_3));  // open: dp
  Hex_Digit_Display hex_digit_display_7 (.value(output_register_1_output_4));  // open: dp
  Stack stack_1 (
    .To_PC(stack_1_to_pc), .Count_minus(controller_sequencer_1_control_word_out_2[0]),
    .Count_plus(controller_sequencer_1_control_word_out[7]), .Ts(controller_sequencer_1_control_word_out[6]),
    .Load_Stack(controller_sequencer_1_control_word_out[5]),
    .Enable_Stack(controller_sequencer_1_control_word_out[4]), .Bus_Output(ram_1_data),
    .Bus_Input(ram_1_data), .Clear_counter(not_2_out), .Clock(and_1_out));
  Hex_Digit_Display hex_digit_display_8 (.value(adder_subtractor_1_out_7[19:16]));  // open: dp
  Adder_Subtractor adder_subtractor_1 (
    .Subtract(controller_sequencer_1_control_word_out[3]), .Lu(controller_sequencer_1_control_word_out[2]),
    .Clear(not_2_out), .Enable(controller_sequencer_1_control_word_out[1]), .Clock(and_1_out),
    .Input(ram_1_data), .Output(ram_1_data), .out_7(adder_subtractor_1_out_7),
    .out_8(adder_subtractor_1_out_8));
  Output_Register output_register_1 (
    .Load(controller_sequencer_1_control_word_out[0]), .Clock(and_1_out), .Input(ram_1_data),
    .Output({output_register_1_output_4, output_register_1_output_3, output_register_1_output_2, output_register_1_output}));
  Hex_Digit_Display hex_digit_display_9 (.value(adder_subtractor_1_out_8[19:16]));  // open: dp
  Hex_Digit_Display hex_digit_display_10 (.value(output_register_1_output_2));  // open: dp
  Hex_Digit_Display hex_digit_display_11 (.value(adder_subtractor_1_out_7[15:12]));  // open: dp
  Hex_Digit_Display hex_digit_display_12 (.value(adder_subtractor_1_out_8[15:12]));  // open: dp
  Hex_Digit_Display hex_digit_display_13 (.value(output_register_1_output[7:4]));  // open: dp
  Hex_Digit_Display hex_digit_display_14 (.value(output_register_1_output[3:0]));  // open: dp
  Hex_Digit_Display hex_digit_display_15 (.value(adder_subtractor_1_out_7[7:4]));  // open: dp
  Hex_Digit_Display hex_digit_display_16 (.value(adder_subtractor_1_out_7[11:8]));  // open: dp
  Hex_Digit_Display hex_digit_display_17 (.value(adder_subtractor_1_out_8[11:8]));  // open: dp
  Hex_Digit_Display hex_digit_display_18 (.value(adder_subtractor_1_out_8[7:4]));  // open: dp
  Hex_Digit_Display hex_digit_display_19 (.value(adder_subtractor_1_out_7[3:0]));  // open: dp
  Hex_Digit_Display hex_digit_display_20 (.value(adder_subtractor_1_out_8[3:0]));  // open: dp

  // Notes on the sheet:
  //   SAP-1s
  //   Control Word
  //   PC
  //   MAR
  //   IR
  //   CU
  //   Output
  //   S
  //   ALU
  //   O
endmodule

module Adder_Subtractor (
  input  Subtract,
  input  Lu,
  input  Clear,
  input  Enable,
  input  Clock,
  input  [19:0] Input,
  output [19:0] out_7,
  output [19:0] out_8,
  output [19:0] Output
);

  wire j_k_ff_1_q;
  wire [19:0] adder_1_out, demultiplexer_1_out0, demultiplexer_1_out1, xor_1_out;

  Demultiplexer #(.select(1), .width(20), .tristate("true")) demultiplexer_1 (
    .out0(demultiplexer_1_out0), .out1(demultiplexer_1_out1), .in(Input), .sel(j_k_ff_1_q));
  J_K_Flip_Flop #(.trigger("rising")) j_k_ff_1 (
    .J(1'b1), .clk(Clock), .K(1'b1), .Q(j_k_ff_1_q), .en(Lu), .reset(Clear));  // open: Qn, preset
  Register #(.width(20), .trigger("rising")) register_1 (
    .D(demultiplexer_1_out0), .en(Lu), .Q(out_8), .clk(Clock), .clr(Clear));
  Register #(.width(20), .trigger("rising")) register_2 (
    .D(demultiplexer_1_out1), .en(Lu), .Q(out_7), .clk(Clock), .clr(Clear));
  assign xor_1_out = out_8 ^ {20{Subtract}};  // XOR_Gate xor_1, 20 bits wide
  assign Output = Enable ? adder_1_out : 20'bz;  // Controlled_Buffer controlled_buffer_1
  Adder #(.width(20)) adder_1 (.a(xor_1_out), .b(out_7), .out(adder_1_out), .cin(Subtract));  // open: cout

  // Notes on the sheet:
  //   Adder/Subtracter
endmodule

module Output_Register (
  input  Load,
  input  Clock,
  input  [19:0] Input,
  output [19:0] Output
);

  Register #(.width(20), .trigger("rising")) register_1 (.D(Input), .en(Load), .Q(Output), .clk(Clock));  // open: clr

  // Notes on the sheet:
  //   Output Register
endmodule

module Program_Counter (
  input  Count,
  input  Lp,
  input  Enable,
  input  [15:0] Bus_Input,
  input  Clock,
  input  Clear,
  output [15:0] Bus_Output
);

  wire not_1_out;
  wire [15:0] counter_1_q;

  Counter #(.width(16), .max(65535), .trigger("rising")) counter_1 (
    .load(Lp), .D(Bus_Input), .count(Count), .Q(counter_1_q), .clk(not_1_out), .clr(Clear));  // open: carry
  not not_1 (not_1_out, Clock);
  assign Bus_Output = Enable ? counter_1_q : 16'bz;  // Controlled_Buffer controlled_buffer_1

  // Notes on the sheet:
  //   Program Counter
endmodule

module Memory_Address_Register (
  input  [15:0] Input,
  input  Clock,
  input  Load,
  output [15:0] RAM_output
);

  Register #(.width(16), .trigger("rising")) register_1 (
    .D(Input), .en(Load), .Q(RAM_output), .clk(Clock));  // open: clr

  // Notes on the sheet:
  //   MAR
endmodule

module Instruction_Register (
  input  [19:0] Input,
  input  Clock,
  input  Load,
  input  Enable,
  input  Clear,
  output [15:0] Bus_Output,
  output [3:0] CS_Output,
  output nHalt
);

  wire [15:0] register_1_q;

  Register #(.width(20), .trigger("rising")) register_1 (
    .D(Input), .en(Load), .Q({CS_Output, register_1_q}), .clk(Clock), .clr(Clear));
  assign Bus_Output = Enable ? register_1_q : 16'bz;  // Controlled_Buffer controlled_buffer_1
  nand nand_1 (nHalt, CS_Output[3], CS_Output[2], CS_Output[1], CS_Output[0]);

  // Notes on the sheet:
  //   Instruction Register
endmodule

module Controller_sequencer (
  input  [3:0] IR_Input,
  input  Clock,
  input  Clear,
  output [5:0] T_State,
  output [19:0] Control_Word_Out
);

  wire and_1_out, nor_1_out, nor_2_out, nor_3_out, not_1_out, or_1_out, or_3_out, t_state_sequencer_1_t6;
  wire [1:0] or_2_out;
  wire [7:0] counter_1_q, multiplexer_1_out, rom_1_data;

  T_State_Sequencer t_state_sequencer_1 (
    .Clock(Clock), .Clear(or_1_out), .T_State(T_State), .T3(or_2_out[1]), .T6(t_state_sequencer_1_t6));
  or or_1 (or_1_out, Clear, and_1_out);
  or or_2 (or_2_out[0], t_state_sequencer_1_t6, and_1_out);
  ROM #(.addrWidth(4), .dataWidth(8)) rom_1 (.addr(IR_Input), .data(rom_1_data));  // open: sel
  Multiplexer #(.select(2), .width(8)) multiplexer_1 (
    .in1({8{1'b0}}), .in2(rom_1_data), .out(multiplexer_1_out), .sel(or_2_out));  // open: in0, in3
  or or_3 (or_3_out, or_2_out[1], or_2_out[0]);
  not not_1 (not_1_out, or_3_out);
  Counter #(.width(8), .max(255), .trigger("falling")) counter_1 (
    .load(or_3_out), .D(multiplexer_1_out), .count(not_1_out), .Q(counter_1_q), .clk(Clock), .clr(Clear));  // open: carry
  and and_1 (and_1_out, nor_1_out, nor_2_out, nor_3_out);
  nor nor_1 (nor_1_out, Control_Word_Out[0], Control_Word_Out[1], Control_Word_Out[2], Control_Word_Out[3], Control_Word_Out[4], Control_Word_Out[5], Control_Word_Out[6], Control_Word_Out[7], Control_Word_Out[8]);
  nor nor_2 (nor_2_out, Control_Word_Out[9], Control_Word_Out[10], Control_Word_Out[11], Control_Word_Out[12], Control_Word_Out[13], Control_Word_Out[14], Control_Word_Out[15], Control_Word_Out[16], Control_Word_Out[17]);
  nor nor_3 (nor_3_out, Control_Word_Out[18], Control_Word_Out[19]);
  ROM #(.addrWidth(8), .dataWidth(20)) rom_2 (.addr(counter_1_q), .data(Control_Word_Out));  // open: sel

  // Notes on the sheet:
  //   Controller/sequencer
  //   T-State Sequencer
  //   Address ROM
  //   contents of rom_1 (hex, n*v repeats v):
  //   3 6 9 f 12 15 18 7*0 c
  //   Control ROM
  //   contents of rom_2 (hex, n*v repeats v):
  //   30000 80000 6000 80 11000 4020 114 14 22 114 14 2a 11 0 0 1a3 12f3 3e3 23a3 3e3 3e3 43a3 3e3 3e3 1a3
  //   e3 2c3
  //   Load: 0000/0
  //   Add: 0001/1
  //   Subtract: 0010/2
  //   Store: 0011/3
  //   Jump: 0100/4
  //   Jump if Zero: 01001/5
  //   Output:1110/E
  //   Halt: 1111/F
  //   Load Indirect (pointer): 0110/6
endmodule

module T_State_Sequencer (
  input  Clock,
  input  Clear,
  output T3,
  output T6,
  output [5:0] T_State
);

  wire d_ff_7_q, not_1_out, undriven, undriven_2;

  not not_1 (not_1_out, Clock);
  D_Flip_Flop #(.trigger("rising")) d_ff_1 (
    .clk(not_1_out), .D(T6), .Q(T_State[5]), .preset(Clear));  // open: Qn, en, reset
  D_Flip_Flop #(.trigger("rising")) d_ff_2 (
    .clk(not_1_out), .D(T_State[5]), .Q(T_State[4]), .reset(Clear));  // open: Qn, preset, en
  D_Flip_Flop #(.trigger("rising")) d_ff_3 (
    .clk(not_1_out), .D(T_State[4]), .Q(T3), .reset(Clear));  // open: Qn, preset, en
  D_Flip_Flop #(.trigger("rising")) d_ff_4 (
    .clk(not_1_out), .D(T3), .Q(T_State[2]), .reset(Clear));  // open: Qn, preset, en
  D_Flip_Flop #(.trigger("rising")) d_ff_5 (
    .clk(not_1_out), .D(T_State[2]), .Q(T_State[1]), .reset(Clear));  // open: Qn, preset, en
  D_Flip_Flop #(.trigger("rising")) d_ff_6 (
    .clk(not_1_out), .D(T_State[1]), .Q(T6), .reset(Clear));  // open: Qn, preset, en
  D_Flip_Flop #(.trigger("rising")) d_ff_7 (
    .clk(undriven), .Q(d_ff_7_q), .reset(undriven_2));  // open: D, Qn, preset, en

  assign {T_State[3], T_State[0]} = {T3, T6};

  // Notes on the sheet:
  //   T-State Sequencer
endmodule

module Stack (
  input  Count_minus,
  input  Count_plus,
  input  Ts,
  input  Load_Stack,
  input  Enable_Stack,
  input  [19:0] Bus_Input,
  input  Clear_counter,
  input  Clock,
  output To_PC,
  output [19:0] Bus_Output
);

  wire and_1_out, and_2_out, nor_1_out, nor_2_out, not_1_out, or_1_out, or_2_out;
  wire [3:0] counter_1_q;
  wire [19:0] ram_1_data;

  or or_1 (or_1_out, Count_minus, Count_plus);
  Counter #(.width(4), .max(15), .trigger("rising")) counter_1 (
    .load(Count_minus), .count(or_1_out), .Q(counter_1_q), .clk(Clock), .clr(Clear_counter));  // open: D, carry
  or or_2 (or_2_out, Enable_Stack, Load_Stack);
  not not_1 (not_1_out, Load_Stack);
  RAM #(.addrWidth(4), .dataWidth(20), .bus("asynch")) ram_1 (
    .addr(counter_1_q), .data(ram_1_data), .sel(or_2_out), .ld(not_1_out));  // open: clr
  nor nor_1 (nor_1_out, ram_1_data[0], ram_1_data[1], ram_1_data[2], ram_1_data[3], ram_1_data[4], ram_1_data[5], ram_1_data[6], ram_1_data[7], ram_1_data[8]);
  and and_1 (and_1_out, nor_1_out, nor_2_out);
  nor nor_2 (nor_2_out, ram_1_data[9], ram_1_data[10], ram_1_data[11], ram_1_data[12], ram_1_data[13], ram_1_data[14], ram_1_data[15], ram_1_data[16], ram_1_data[17]);
  nor nor_3 (nor_2_out, ram_1_data[18], ram_1_data[19]);
  assign ram_1_data = Load_Stack ? Bus_Input : 20'bz;  // Controlled_Buffer controlled_buffer_1
  assign Bus_Output = Enable_Stack ? ram_1_data : 20'bz;  // Controlled_Buffer controlled_buffer_2
  and and_2 (and_2_out, and_1_out, Ts);

  // Notes on the sheet:
  //   Stack pointer
  //   Stack
endmodule
